# Fritzing sketch Schematic (saved by Fritzing 0.9.1b)
breadboards: 1

parts:
  NeoPixel_Ring = Neopixel Ring 16
  FLORA = Adafruit_Flora
  R1 = Resistor [tolerance=±5% resistance=10k package="1206 [SMD]"]
  S1 = SWITCH-MOMENTARY-2 [package=tactile-pth-12mm]
  To_Arduino_Mega = Screw terminal - 2 pins [package=THT]

nets:
  N1: NeoPixel_Ring.GND, FLORA.connector11, R1.Pin_1
  N2: NeoPixel_Ring.VCC, FLORA.connector8, S1.1
  N3: NeoPixel_Ring.IN, FLORA.connector9
  N4: FLORA.connector10, R1.Pin_0, S1.2
  N5: FLORA.connector12, To_Arduino_Mega.pin2

notes:
  D9 sends a HIGH signal when sequence is complete. This pin should go to a digital input on the primary arduino mega circuit

custom parts:
  Neopixel Ring 16: Neopixel Ring x16
